# Fritzing sketch Arduino_Serra (saved by Fritzing 0.8.7b)
circuit board: 8.46667cm x 5.64444cm
breadboards: 1

parts:
  Componente1 = Arduino Uno (Rev3)
  DHT1 = DHT11 Humitidy and Temperature Sensor  # not connected
  U1 = ENCODER_2LED [package=encoder_led_2]  # not connected
  LCD1 = LCD screen  # not connected
  M1 = DC Motor  # not connected
  Componente2 = Real Time Clock Module - DS1307 RTC Breakout Board  # not connected
  R1 = PHOTOCELL [package=photocell-kit]  # not connected
  R2 = Trimmer Potentiometer [maximum_resistance=100kΩ package=THT]  # not connected
  J1 = Basic Servo
  Componente3 = Arduino Nano (Rev3.0)  # not connected

nets:
  N1: Componente1.D9_PWM, J1.pulse
  5V: Componente1.5V, J1.vcc
  GND: Componente1.GND, J1.gnd

custom parts:
  DHT11 Humitidy and Temperature Sensor: DHT11 Humidity and Temperature Sensor
